// Digital circuit lab05_pipelined.dig as structural Verilog
module lab05_pipelined (
  input  clk,
  input  rst,
  output [31:0] PC,
  output [5:0] opcode,
  output [4:0] src1__addr,
  output [31:0] src1__out,
  output [4:0] src2__addr,
  output [31:0] src2__out,
  output [4:0] dst__addr,
  output [31:0] dst__data
);

  wire alu__src, br, EX_MEM_p10, EX_MEM_p13, ID_EX_p12, ID_EX_p13, IF_ID_p5, mem__read, mem__write,
       MEM_WB_p4, PCSrc, reg__dst, reg__write, u_alu_3_zero;
  wire [1:0] alu__op, u_control_unit_alu_op, u_control_unit_reg_write;
  wire [1:1] MEM_WB_p7;
  wire [2:0] u_control_unit_branch;
  wire [3:0] u_alu_control_alu_control, u_control_unit_reg_dst;
  wire [4:0] multiplexer_3_out, undriven, undriven_2;
  wire [15:0] instr;
  wire [31:0] bitextender_1_out, branchAddr, cpumemory_d2, data__val, ID_EX_p15, ID_EX_p16, ID_EX_p17,
       ID_EX_p18, incrPC, mem__addr, mem__data, MEM_WB_p8, MEM_WB_p9, multiplexer_1_out, multiplexer_2_out,
       src2, u_alu_2_result, u_alu_3_result;

  Multiplexer #(.Bits(32)) multiplexer_1 (.sel(PCSrc), .in_0(incrPC), .in_1(branchAddr), .out(multiplexer_1_out));
  gen_register #(.applicationType("IVERILOG"), .CodeFile("./gen_register.v")) u_gen_register (
    .clk(clk), .rst(rst), .write_en(clk), .data_in(multiplexer_1_out), .data_out(PC));
  alu #(.applicationType("IVERILOG"), .CodeFile("./alu.v")) u_alu (
    .alu_control(4'b0010), .A(PC), .B(32'h4), .result(incrPC));  // open: zero
  RAMDualAccess #(.AddrBits(8), .isProgramMemory("true"), .Bits(32)) cpumemory (
    .str(mem__write), .C(clk), .ld(mem__read), .A1(mem__addr[7:0]), .Din1(mem__data), .A2(PC[9:2]),
    .D1(data__val), .D2(cpumemory_d2));
  // if_id IF_ID: pin names not known; wires that end beside it: incrPC, cpumemory_d2, clk, clk, IF_ID_p5, {opcode, src1__addr, src2__addr, instr}
  control_unit #(.applicationType("IVERILOG"), .CodeFile("./control_unit.v")) u_control_unit (
    .instr_op(opcode), .reg_write(u_control_unit_reg_write[0]), .mem_to_reg(u_control_unit_reg_write[1]),
    .branch(u_control_unit_branch[0]), .mem_read(u_control_unit_branch[1]),
    .mem_write(u_control_unit_branch[2]), .reg_dst(u_control_unit_reg_dst[0]),
    .alu_op(u_control_unit_alu_op), .alu_src(u_control_unit_reg_dst[3]));
  BitExtender #(.inputBits(16), .outputBits(32)) bitextender_1 (.in(instr), .out(bitextender_1_out));
  cpu_registers #(.applicationType("IVERILOG"), .CodeFile("./cpu_registers.v")) u_cpu_registers (
    .clk(clk), .rst(rst), .write_en(reg__write), .src1_addr(src1__addr), .src2_addr(src2__addr),
    .dst_addr(dst__addr), .data_in(dst__data), .src1_out(src1__out), .src2_out(src2));
  // id_ex ID_EX: pin names not known; wires that end beside it: u_control_unit_reg_write, u_control_unit_branch, {u_control_unit_reg_dst[3], u_control_unit_alu_op, u_control_unit_reg_dst[0]}, IF_ID_p5, src1__out, src2, bitextender_1_out, src2__addr, instr[15:11], clk, clk, ID_EX_p12, ID_EX_p13, {alu__src, alu__op, reg__dst}, ID_EX_p15, ID_EX_p16, ID_EX_p17, ID_EX_p18
  Multiplexer #(.Bits(32)) multiplexer_2 (.sel(alu__src), .in_0(ID_EX_p17), .in_1(ID_EX_p18), .out(multiplexer_2_out));
  Multiplexer #(.Bits(5)) multiplexer_3 (.sel(reg__dst), .in_0(undriven), .in_1(undriven_2), .out(multiplexer_3_out));
  alu_control #(.applicationType("IVERILOG"), .CodeFile("./alu_control.v")) u_alu_control (
    .funct(ID_EX_p18[5:0]), .alu_op(alu__op), .alu_control(u_alu_control_alu_control));
  alu #(.applicationType("IVERILOG"), .CodeFile("./alu.v")) u_alu_2 (
    .alu_control(4'b0010), .A(ID_EX_p15), .B({ID_EX_p18[31:2], 2'b00}), .result(u_alu_2_result));  // open: zero
  alu #(.applicationType("IVERILOG"), .CodeFile("./alu.v")) u_alu_3 (
    .A(ID_EX_p16), .B(multiplexer_2_out), .alu_control(u_alu_control_alu_control), .zero(u_alu_3_zero),
    .result(u_alu_3_result));
  // ex_mem EX_MEM: pin names not known; wires that end beside it: ID_EX_p12, ID_EX_p13, u_alu_2_result, u_alu_3_zero, u_alu_3_result, ID_EX_p17, multiplexer_3_out, clk, clk, EX_MEM_p10, {mem__write, mem__read, br}, branchAddr, EX_MEM_p13, mem__addr
  and and_1 (PCSrc, br, EX_MEM_p13);
  // mem_wb MEM_WB: pin names not known; wires that end beside it: EX_MEM_p10, data__val, mem__addr, MEM_WB_p4, clk, clk, {MEM_WB_p7[1], reg__write}, MEM_WB_p8, MEM_WB_p9
  Multiplexer #(.Bits(32)) multiplexer_4 (.sel(MEM_WB_p7[1]), .in_0(MEM_WB_p9), .in_1(MEM_WB_p8), .out(dst__data));

  assign src2__out = src1__out;

  // Other names for the same wires on the sheet: instr[31:16] = {opcode, src1__addr, src2__addr};
  //   reg__data[31:0] = dst__data; src1[31:0] = src1__out

  // Notes on the sheet:
  //   Inputs
  //   PC
  //   Outputs for testing
endmodule
